# Fritzing sketch sketch (saved by Fritzing 0.9.4)

parts:
  Composant1 = Arduino Nano (Rev3.0)
  U1 = SLIDER [package=slider]
  U2 = SLIDER [package=slider]
  M2 = DC Motor
  M3 = DC Motor
  U4 = SLIDER [package=slider]
  M4 = DC Motor
  S1 = Pushbutton [package="[THT]"]
  Composant2 = Adafruit TCA9548A
  OLED1 = OLED 128x64 I2C Monochrome Display
  OLED2 = OLED 128x64 I2C Monochrome Display
  OLED3 = OLED 128x64 I2C Monochrome Display
  OLED4 = OLED 128x64 I2C Monochrome Display
  U5 = L9110 H-bridge module [part_number="L9110 H-bridge"]
  M1 = DC Motor
  U6 = L9110 H-bridge module [part_number="L9110 H-bridge"]
  U9 = BATTERY-2 [package=battery-aa]
  U10 = BATTERY-2 [package=battery-aa]
  U11 = BATTERY-2 [package=battery-aa]
  U12 = BATTERY-2 [package=battery-aa]
  LED1 = LED - 5mm [color="Red (633nm)" package="5 mm [THT]"]
  Q1 = Basic FET N-Channel [package="DPak [SMD]"]
  U13 = PCF8574 [package="DIP16 [THT]"]
  S10 = Pushbutton [package="[THT]"]
  S11 = Pushbutton [package="[THT]"]
  S12 = Pushbutton [package="[THT]"]
  R1 = Resistor [tolerance=±5% resistance=10k package="0603 [SMD]"]
  R2 = Resistor [tolerance=±5% resistance=10k package="0603 [SMD]"]
  R3 = Resistor [tolerance=±5% resistance=10k package="0603 [SMD]"]
  R4 = Resistor [tolerance=±5% resistance=10k package="0603 [SMD]"]
  LED5 = LED - 5mm [color="Red (633nm)" package="5 mm [THT]"]
  LED6 = LED - 5mm [color="Red (633nm)" package="5 mm [THT]"]
  LED7 = LED - 5mm [color="Red (633nm)" package="5 mm [THT]"]
  S13 = Pushbutton [package="[THT]"]
  S14 = Pushbutton [package="[THT]"]
  R5 = Resistor [tolerance=±5% resistance=10k package="0603 [SMD]"]
  R6 = Resistor [tolerance=±5% resistance=10k package="0603 [SMD]"]
  U3 = SLIDER [package=slider]
  R7 = Resistor [tolerance=±5% resistance=4.3k package="2512 [SMD]"]

nets:
  GND: Composant1.GND, U1.E, U2.E, U4.E, S1.Pin_1, S1.Pin_2, Composant2.GND, Composant2.A0, Composant2.A1, Composant2.A2, OLED1.GND, OLED2.GND, OLED3.GND, OLED4.GND, U11.-1, LED1.cathode, Q1.source, U13.GND, S10.Pin_1, S10.Pin_2, S11.Pin_1, S11.Pin_2, S12.Pin_1, S12.Pin_2, LED5.cathode, LED6.cathode, LED7.cathode, S14.Pin_1, S14.Pin_2, U3.E
  N1: Composant1.D2, S13.Pin_3, S13.Pin_4, R6.Pin_0
  N2: Composant1.D3, S14.Pin_3, S14.Pin_4, R5.Pin_0
  N3: Composant1.D4, R7.Pin_0
  N4: Composant1.D5, U6.A-IB
  N5: Composant1.D6, U6.A-IA
  N6: Composant1.D7, U6.B-IB
  N7: Composant1.D8, U6.B-IA
  N8: Composant1.D9, U5.A-IB
  N9: Composant1.D10, U5.A-IA
  N10: Composant1.D11/MOSI, U5.B-IB
  N11: Composant1.D12/MISO, U5.B-IA
  5V: Composant1.5V, U1.A, U2.A, U4.A, Composant2.VCC, U13.VCC, R1.Pin_1, R2.Pin_1, R3.Pin_1, R4.Pin_1, R5.Pin_1, R6.Pin_1, U3.A
  i2c scl: Composant1.A5, Composant2.INPUTSCL, U13.SCL
  i2c sda: Composant1.A4, Composant2.INPUTSDA, U13.SDA
  N12: Composant1.A3, U4.S
  N13: Composant1.A2, U3.S
  N14: Composant1.A1, U2.S
  N15: Composant1.A0, U1.S
  3.3V: Composant1.3V3, OLED1.VDD, OLED2.VDD, OLED3.VDD, OLED4.VDD
  N16: M2.pin_1, U5.MOTOR_A-B
  N17: M2.pin_2, U5.MOTOR_A-A
  N18: M3.pin_1, U6.MOTOR_B-B
  N19: M3.pin_2, U6.MOTOR_B-A
  N20: M4.pin_1, U6.MOTOR_A-B
  N21: M4.pin_2, U6.MOTOR_A-A
  N22: S1.Pin_3, S1.Pin_4, U13.P0, R1.Pin_0
  N23: Composant2.3SDA, OLED2.SDA
  N24: Composant2.3SCL, OLED2.SCK
  N25: Composant2.5SDA, OLED3.SDA
  N26: Composant2.5SCL, OLED3.SCK
  N27: Composant2.7SDA, OLED4.SDA
  N28: Composant2.7SCL, OLED4.SCK
  N29: Composant2.1SDA, OLED1.SDA
  N30: Composant2.1SCL, OLED1.SCK
  GND_2: U5.GND, U6.GND, Q1.drain
  VCC: U5.VCC, U6.VCC, U9.+1
  N31: U5.MOTOR_B-A, M1.pin_2
  N32: U5.MOTOR_B-B, M1.pin_1
  N33: U9.-1, U10.+1
  N34: U10.-1, U12.+1
  N35: U11.+1, U12.-1
  N36: LED1.anode, U13.P4
  N37: U13.P1, S10.Pin_3, S10.Pin_4, R2.Pin_0
  N38: U13.P2, S11.Pin_3, R3.Pin_0
  N39: U13.P3, S12.Pin_3, S12.Pin_4, R4.Pin_0
  N40: U13.P5, LED5.anode
  N41: U13.P6, LED6.anode
  N42: U13.P7, LED7.anode

notes:
  APP2
  APP1
  MIC
  MASTER
  Mute switch & LED indicator for each channel >
  Channel select switches

custom parts:
  Adafruit TCA9548A: You just found the perfect I2C sensor, and you want to wire up two or three or more of them to your Arduino when you realize "Uh oh, this chip has a fixed I2C address, and from what I know about I2C, you cannot have two devices with the same address on the same SDA/SCL pins!" Are you out of luck? You would be, if you didn't have this ultra-cool TCA9548A 1-to-8 I2C multiplexer! Finally, a way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
